# Fritzing sketch tarefa01 (saved by Fritzing 0.9.3b)
breadboards: 1

parts:
  Componente1 = Arduino Uno (Rev3)
  S1 = Pushbutton [package="[THT]"]
  S2 = Pushbutton [package="[THT]"]
  R1 = Resistor [tolerance=±5% resistance=330 package=THT]
  LED1 = LED - 5mm [color="Red (633nm)" package="5 mm [THT]"]
  LED2 = LED - 5mm [color="Red (633nm)" package="5 mm [THT]"]
  LED3 = LED - 5mm [color="Red (633nm)" package="5 mm [THT]"]
  R2 = Resistor [tolerance=±5% resistance=330k package=THT]
  R3 = Resistor [tolerance=±5% resistance=330k package=THT]

nets:
  N1: Componente1.D8, R1.Pin_1
  N2: Componente1.GND, LED1.cathode, R2.Pin_0, R3.Pin_0
  N3: Componente1.D2, S1.Pin_1, S1.Pin_2, LED2.anode
  N4: Componente1.D3_PWM, S2.Pin_1, S2.Pin_2, LED3.anode
  N5: Componente1.5V, S1.Pin_3, S1.Pin_4, S2.Pin_3, S2.Pin_4
  N6: R1.Pin_0, LED1.anode
  N7: LED2.cathode, R3.Pin_1
  N8: LED3.cathode, R2.Pin_1

// code stored in the sketch: tarefa01.ino
#include <Arduino.h>
#include <Wire.h>
#include <LiquidCrystal_I2C.h>
//LCD I2C for display delay LED and state
LiquidCrystal_I2C i2cLcd(0x27,2,1,0,4,5,6,7,3,POSITIVE);
//debaunce | LOCK LED | oldStateUp | oldStateDown
uint8_t states = 0;
uint64_t timeLed;
uint16_t delayLed = 1000;//milliseconds
uint64_t timeButtonDown;
uint64_t timeButtonUp;
uint64_t holdButtons;

void delayLedPrint(void){
	String 	msg = "";
  if(states & (1 << 2)){
    msg += "    LOCK LED: ";
    if(PINB & (1 << PB0)){
      msg += "ON    ";
    }else{
      msg += "OFF   ";
    }
  }else{
    msg += "DELAY LED: ";
  	if(delayLed < 10000){
  		msg += "0";
  	}
  	if(delayLed < 10000){
  		msg += "0";
  	}
  	if(delayLed < 1000){
  		msg += "0";
  	}
  	if(delayLed < 100){
  		msg += "0";
  	}
  	if(delayLed < 10){
  		msg += "0";
  	}
  	msg += delayLed;
  	msg += "ms ";
  }
  i2cLcd.setCursor(0,3);
  i2cLcd.print(msg);
  Serial.print(msg);
  Serial.println();
  timeLed = millis();
}

void setup() {
  DDRD  &= ~(1 << PD2);PORTD &= ~(1 << PD2);//pinMode(2,INPUT);//button DOWN delay LED
  DDRD  &= ~(1 << PD4);PORTD &= ~(1 << PD4);//pinMode(4,INPUT);//button UP delay LED
	DDRB  &= ~(1 << PB0);PORTB &= ~(1 << PB0);//pinMode(8,OUTPUT);digitalWrite(8,LOW);//set LED to LOW
  i2cLcd.begin(20,4);
  i2cLcd.clear();
  Serial.begin(115200);
  i2cLcd.setCursor(0,0);
  i2cLcd.print(" Wellington Rodrigo ");
  Serial.print(" Wellington Rodrigo ");
  Serial.println();
  i2cLcd.setCursor(0,1);
  i2cLcd.print(" Software Embarcado ");
  Serial.print(" Software Embarcado ");
  Serial.println();
  i2cLcd.setCursor(0,2);
  i2cLcd.print("     TAREFA  01     ");
  Serial.print("     TAREFA  01     ");
  Serial.println();
  delayLedPrint();
  //inicia ativando todos os bits para do debaunce  248ms
  states = (1 << 7) | (1 << 6) | (1 << 5) | (1 << 4) | (1 << 3);
}

void loop() {
  while(states & (1 << 2));//caso seja setado para true trava a execução
  if(millis() >= timeLed+delayLed){
    timeLed = millis();
		//faz o LED piscar
		PORTB ^= (1 << PB0);//ledState = ~ledState;digitalWrite(8,ledState);
  }
  //buttons control
	uint8_t curButtons = (PIND & B00001100) >> 2;//máscara para pegar os pinos PD2 e PD3
	switch(states & B00000011){
    case 0://DOWN OFF | UP OFF
			switch(curButtons){
				case 3:
					if(millis() >= timeButtonDown+((states & B11111000) >> 2) && millis() >= timeButtonDown+((states & B11111000) >> 2)){
						holdButtons = millis();
						states ^= (1 << 0);
						states ^= (1 << 1);
					}
					break;
				case 2:
					if(millis() >= timeButtonDown+((states & B11111000) >> 2)){
						timeButtonUp = millis();
						if(delayLed < 10000){
							delayLed += 100;
						}
						delayLedPrint();
						states ^= (1 << 1);
					}
					break;
				case 1:
					if(millis() >= timeButtonDown+((states & B11111000) >> 2)){
						timeButtonDown = millis();
						if(delayLed > 100){
							delayLed -= 100;
						}
						delayLedPrint();
						states ^= (1 << 0);
					}
					break;
			};
      break;
    case 1://DOWN ON  | UP OFF
			switch(curButtons){
				case 3:
					if(millis() >= timeButtonDown+((states & B11111000) >> 2) && millis() >= timeButtonDown+((states & B11111000) >> 2)){
						holdButtons = millis();
						states ^= (1 << 1);
					}
					break;
				case 2:
					if(millis() >= timeButtonDown+((states & B11111000) >> 2)){
						timeButtonUp = millis();
						if(delayLed < 10000){
							delayLed += 100;
						}
						delayLedPrint();
	          states ^= (1 << 0);
						states ^= (1 << 1);
					}
					break;
				case 1:
					if(millis() >= timeButtonDown+(states & B11111000)){
            timeButtonDown = millis();
	          if(delayLed > 100){
							delayLed -= 100;
						}
						delayLedPrint();
          }
					break;
				case 0:
					states ^= (1 << 0);
					break;
			};
      break;
    case 2://DOWN OFF | UP ON
			switch(curButtons){
				case 3:
					if(millis() >= timeButtonDown+((states & B11111000) >> 2) && millis() >= timeButtonDown+((states & B11111000) >> 2)){
						holdButtons = millis();
						states ^= (1 << 0);
					}
					break;
				case 2:
          if(millis() >= timeButtonUp+(states & B11111000)){
            timeButtonUp = millis();
	          if(delayLed < 10000){
							delayLed += 100;
						}
						delayLedPrint();
          }
					break;
				case 1:
					if(millis() >= timeButtonUp+((states & B11111000) >> 2)){
						timeButtonDown = millis();
						if(delayLed < 10000){
							delayLed -= 100;
						}
						delayLedPrint();
	          states ^= (1 << 0);
						states ^= (1 << 1);
					}
					break;
				case 0:
					states ^= (1 << 1);
					break;
			};
      break;
    case 3://DOWN ON  | UP ON
			switch(curButtons){
				case 0:
					if(millis()>=holdButtons+500){
	          states |= (1 << 2);
						delayLedPrint();
	        }
					states ^= (1 << 0);
					states ^= (1 << 1);
					break;
				case 1:
					if(millis()>=holdButtons+500){
	          states |= (1 << 2);
						delayLedPrint();
	        }
					states ^= (1 << 0);
					break;
				case 2:
					if(millis()>=holdButtons+500){
	          states |= (1 << 2);
						delayLedPrint();
	        }
					states ^= (1 << 1);
					break;
			};
			break;
  };
}

// code stored in the sketch: trabalho01.ino
#include <Arduino.h>
#include <Wire.h>
#include <LiquidCrystal_I2C.h>
//LCD I2C for display delay LED and state
LiquidCrystal_I2C i2cLcd(0x27,2,1,0,4,5,6,7,3,POSITIVE);
//debaunce | LOCK LED | oldStateUp | oldStateDown
uint8_t states = 0;
uint64_t timeLed;
uint16_t delayLed = 1000;//milliseconds
uint64_t timeButtonDown;
uint64_t timeButtonUp;
uint64_t holdButtons;

void delayLedPrint(void){
	String 	msg = "";
  if(states & (1 << 2)){
    msg += "    LOCK LED: ";
    if(PINB & (1 << PB0)){
      msg += "ON    ";
    }else{
      msg += "OFF   ";
    }
  }else{
    msg += "DELAY LED: ";
  	if(delayLed < 10000){
  		msg += "0";
  	}
  	if(delayLed < 10000){
  		msg += "0";
  	}
  	if(delayLed < 1000){
  		msg += "0";
  	}
  	if(delayLed < 100){
  		msg += "0";
  	}
  	if(delayLed < 10){
  		msg += "0";
  	}
  	msg += delayLed;
  	msg += "ms ";
  }
  i2cLcd.setCursor(0,3);
  i2cLcd.print(msg);
  Serial.print(msg);
  Serial.println();
  timeLed = millis();
}

void setup() {
  DDRD  &= ~(1 << PD2);PORTD &= ~(1 << PD2);//pinMode(2,INPUT);//button DOWN delay LED
  DDRD  &= ~(1 << PD4);PORTD &= ~(1 << PD4);//pinMode(4,INPUT);//button UP delay LED
	DDRB  &= ~(1 << PB0);PORTB &= ~(1 << PB0);//pinMode(8,OUTPUT);digitalWrite(8,LOW);//set LED to LOW
  i2cLcd.begin(20,4);
  i2cLcd.clear();
  Serial.begin(115200);
  i2cLcd.setCursor(0,0);
  i2cLcd.print(" Wellington Rodrigo ");
  Serial.print(" Wellington Rodrigo ");
  Serial.println();
  i2cLcd.setCursor(0,1);
  i2cLcd.print(" Software Embarcado ");
  Serial.print(" Software Embarcado ");
  Serial.println();
  i2cLcd.setCursor(0,2);
  i2cLcd.print("     TAREFA  01     ");
  Serial.print("     TAREFA  01     ");
  Serial.println();
  delayLedPrint();
  //inicia ativando todos os bits para do debaunce  248ms
  states = (1 << 7) | (1 << 6) | (1 << 5) | (1 << 4) | (1 << 3);
}

void loop() {
  while(states & (1 << 2));//caso seja setado para true trava a execução
  if(millis() >= timeLed+delayLed){
    timeLed = millis();
		//faz o LED piscar
		PORTB ^= (1 << PB0);//ledState = ~ledState;digitalWrite(8,ledState);
  }
  //buttons control
	uint8_t curButtons = (PIND & B00001100) >> 2;//máscara para pegar os pinos PD2 e PD3
	switch(states & B00000011){
    case 0://DOWN OFF | UP OFF
			switch(curButtons){
				case 3:
					if(millis() >= timeButtonDown+((states & B11111000) >> 2) && millis() >= timeButtonDown+((states & B11111000) >> 2)){
						holdButtons = millis();
						states ^= (1 << 0);
						states ^= (1 << 1);
					}
					break;
				case 2:
					if(millis() >= timeButtonDown+((states & B11111000) >> 2)){
						timeButtonUp = millis();
						if(delayLed < 10000){
							delayLed += 100;
						}
						delayLedPrint();
						states ^= (1 << 1);
					}
					break;
				case 1:
					if(millis() >= timeButtonDown+((states & B11111000) >> 2)){
						timeButtonDown = millis();
						if(delayLed > 100){
							delayLed -= 100;
						}
						delayLedPrint();
						states ^= (1 << 0);
					}
					break;
			};
      break;
    case 1://DOWN ON  | UP OFF
			switch(curButtons){
				case 3:
					if(millis() >= timeButtonDown+((states & B11111000) >> 2) && millis() >= timeButtonDown+((states & B11111000) >> 2)){
						holdButtons = millis();
						states ^= (1 << 1);
					}
					break;
				case 2:
					if(millis() >= timeButtonDown+((states & B11111000) >> 2)){
						timeButtonUp = millis();
						if(delayLed < 10000){
							delayLed += 100;
						}
						delayLedPrint();
	          states ^= (1 << 0);
						states ^= (1 << 1);
					}
					break;
				case 1:
					if(millis() >= timeButtonDown+(states & B11111000)){
            timeButtonDown = millis();
	          if(delayLed > 100){
							delayLed -= 100;
						}
						delayLedPrint();
          }
					break;
				case 0:
					states ^= (1 << 0);
					break;
			};
      break;
    case 2://DOWN OFF | UP ON
			switch(curButtons){
				case 3:
					if(millis() >= timeButtonDown+((states & B11111000) >> 2) && millis() >= timeButtonDown+((states & B11111000) >> 2)){
						holdButtons = millis();
						states ^= (1 << 0);
					}
					break;
				case 2:
          if(millis() >= timeButtonUp+(states & B11111000)){
            timeButtonUp = millis();
	          if(delayLed < 10000){
							delayLed += 100;
						}
						delayLedPrint();
          }
					break;
				case 1:
					if(millis() >= timeButtonUp+((states & B11111000) >> 2)){
						timeButtonDown = millis();
						if(delayLed < 10000){
							delayLed -= 100;
						}
						delayLedPrint();
	          states ^= (1 << 0);
						states ^= (1 << 1);
					}
					break;
				case 0:
					states ^= (1 << 1);
					break;
			};
      break;
    case 3://DOWN ON  | UP ON
			switch(curButtons){
				case 0:
					if(millis()>=holdButtons+500){
	          states |= (1 << 2);
						delayLedPrint();
	        }
					states ^= (1 << 0);
					states ^= (1 << 1);
					break;
				case 1:
					if(millis()>=holdButtons+500){
	          states |= (1 << 2);
						delayLedPrint();
	        }
					states ^= (1 << 0);
					break;
				case 2:
					if(millis()>=holdButtons+500){
	          states |= (1 << 2);
						delayLedPrint();
	        }
					states ^= (1 << 1);
					break;
			};
			break;
  };
}
