# Fritzing sketch tarefa03-05 (saved by Fritzing 0.9.3b)
breadboards: 2

parts:
  SW-1 = Vibration sensor module
  M1 = fc-51 [package=THT]
  LCM1602_IIC1 = LCM1602 IIC [part_number="LCM1602 IIC" chip_label="LCM1602 IIC" package="DIP (Dual Inline) [THT]"]
  LCD1 = LCD screen
  Componente1 = Arduino Uno (Rev3)
  J1 = Basic Servo
  BB_PWR1 = Toaster Bread Board Dual Supply [package="DIP (Dual Inline) [THT]"]
  J2 = Basic Force Sensing Resistor (FSR) [package=THT]
  LED1 = LED - 5mm [color="White (4500K)" package="5 mm [THT]"]
  R1 = Resistor [tolerance=±5% resistance=330 package=THT]
  R2 = Resistor [tolerance=±5% resistance=10k package=THT]
  R3 = Resistor [tolerance=±5% resistance=330 package=THT]
  R4 = Resistor [tolerance=±5% resistance=330 package=THT]
  LED2 = LED - 5mm [color="Red (660nm)" package="5 mm [THT]"]
  LED3 = LED - 5mm [color="Red (660nm)" package="5 mm [THT]"]  # not connected
  S1 = Pushbutton [package="[THT]"]
  S2 = Pushbutton [package="[THT]"]

nets:
  VCC: SW-1.vcc, M1.pin3, LCM1602_IIC1.VCC, Componente1.5V, J2.pin_0, S1.Pin_3, S1.Pin_4, S2.Pin_3, S2.Pin_4
  GND: SW-1.Ground, M1.pin2, LCM1602_IIC1.GND, Componente1.GND, R1.Pin_0, R2.Pin_0, R3.Pin_0, R4.Pin_0
  N1: SW-1.Digital_output, Componente1.D5_PWM
  N2: M1.pin1, Componente1.D4
  VSS: LCM1602_IIC1.VSS, LCD1.VSS
  VDD: LCM1602_IIC1.VDD, LCD1.VDD
  N3: LCM1602_IIC1.V0, LCD1.V0
  N4: LCM1602_IIC1.RS, LCD1.RS
  N5: LCM1602_IIC1.RW, LCD1.R/W
  N6: LCM1602_IIC1.E, LCD1.E
  N7: LCM1602_IIC1.D0, LCD1.DB0
  N8: LCM1602_IIC1.D1, LCD1.DB1
  N9: LCM1602_IIC1.D2, LCD1.DB2
  N10: LCM1602_IIC1.D3, LCD1.DB3
  N11: LCM1602_IIC1.D4, LCD1.DB4
  N12: LCM1602_IIC1.D5, LCD1.DB5
  N13: LCM1602_IIC1.D6, LCD1.DB6
  N14: LCM1602_IIC1.D7, LCD1.DB7
  N15: LCM1602_IIC1.A, LCD1.LED+
  N16: LCM1602_IIC1.K, LCD1.LED-
  N17: LCM1602_IIC1.SDA, Componente1.A4/SDA
  N18: LCM1602_IIC1.SCL, Componente1.A5/SCL
  N19: LCM1602_IIC1.LED_A, LCM1602_IIC1.LED_B
  N20: Componente1.D9_PWM, J1.pulse
  N21: Componente1.D2, S2.Pin_1, S2.Pin_2
  N22: Componente1.D3_PWM, LED2.anode, S1.Pin_1, S1.Pin_2
  N23: Componente1.D6_PWM, Componente1.3V3
  N24: Componente1.D7, J2.pin_1, LED1.anode, R2.Pin_1
  GND_2: J1.gnd, BB_PWR1.GND
  N25: J1.vcc, BB_PWR1.VO1
  N26: LED1.cathode, R1.Pin_1
  N27: R4.Pin_1, LED2.cathode

custom parts:
  Vibration sensor module: Single-roller type full induction trigger switch. When no vibration or tilt, the product is ON conduction state, and in the steady state, when a vibration or tilt, the switch will be rendered instantly disconnect the conductive resistance increases, generating a current pulse signal, thereby triggering circuit. The default state of the swith is close Digital output Supply voltage:3.3V-5V On-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
  LCM1602 IIC: I2C-Module to use a 1602 or 2004 LCD on with the wire.h libory Serial LCD Modul
  Toaster Bread Board Dual Supply: Toaster is dual output USB step up power supply module designed to fit snuggly into a breadboard. It is powered by a single 5V USB port or charger and outputs three voltages simultaneously, these being 3.3V, 5V and a variable supply which is capable of 5V to 16V.

// code stored in the sketch: tarefa03-05.ino
/* Cáculo para estouro do timer
 * Estouro = Timer1_cont x prescaler x ciclo de máquina
 * Ciclo de máquina = 1/Fosc = 1/16E6 = 62,5ns = 62,5E-9s
 * Estouro = 15625 x 1024 x 62,5E-9 = 1s
*/
#include <Arduino.h>
#include <Wire.h>
#include <Servo.h>
#include <LiquidCrystal_I2C.h>
#define SETTING "SETTING"
#define NORMAL  "       "
#define TELA 1
//LCD I2C for display delay LED and states
LiquidCrystal_I2C i2cLcd(0x27,2,1,0,4,5,6,7,3,POSITIVE);
//Servo:
Servo servoMotor;//usa o timer1 necessário modificar para usar outro timer
uint64_t timeButtonHora;
uint64_t timeButtonMinuto;
uint64_t holdButtons;
uint64_t timeMotor;
//intervalo | SET CLOCK | oldStateMinuto | oldStateHora | oldMotor
uint8_t states  = 0x00;
//Cada digito do Relógio
uint8_t seg     = 0;
uint8_t segundo = 0;
uint8_t telaOn  = TELA;
                //  UNIM|DEZM|UNIH|DEZH
uint8_t clock[4] = {0x00,0x00,0x00,0x00};

void displayPrint(){
  String msg = "";
  msg += clock[3];
  msg += clock[2];
  msg += ":";
  msg += clock[1];
  msg += clock[0];
  i2cLcd.setBacklight(telaOn);
  i2cLcd.setCursor(2,3);
  i2cLcd.print(msg);
  Serial.print("  ");
  Serial.print(msg);
  msg = "";
  if(states & (1 << 3)){
    msg += SETTING;
  }else{
    msg += NORMAL;
  }
  i2cLcd.setCursor(10,3);
  i2cLcd.print(msg);
  Serial.print("    ");
  Serial.print(msg);
  Serial.println();
  PORTB &= ~(1 << PB5);//apaga LED_BUILTIN
}

void setup() {
  DDRD  &= ~(1 << PD2);PORTD &= ~(1 << PD2);//pinMode(2,INPUT);//botao da hora
  DDRD  &= ~(1 << PD3);PORTD &= ~(1 << PD3);//pinMode(3,INPUT);//botao do minuto
  DDRD  &= ~(1 << PD4);PORTD &= ~(1 << PD4);//pinMode(4,INPUT);//infrared sensor
  DDRD  &= ~(1 << PD5);PORTD &= ~(1 << PD5);//pinMode(5,INPUT);//vibration sensor
  DDRB  |=  (1 << PB5);PORTB |=  (1 << PB5);//pinMode(13,OUTPUT);digitalWrite(13,HIGH);//LED_BUILTIN
  ACSR   = 0;//ativar comparador analógico
  servoMotor.attach(9);//define servo motor PWM no pino 9
  i2cLcd.begin(20,4);
  i2cLcd.clear();
  Serial.begin(115200);
  i2cLcd.setCursor(0,0);
  i2cLcd.print(" Wellington Rodrigo ");
  Serial.print(" Wellington Rodrigo ");
  Serial.println();
  i2cLcd.setCursor(0,1);
  i2cLcd.print(" Software Embarcado ");
  Serial.print(" Software Embarcado ");
  Serial.println();
  i2cLcd.setCursor(0,2);
  i2cLcd.print("  TAREFA  02/03/05  ");
  Serial.print("  TAREFA  02/03/05  ");
  Serial.println();
  displayPrint();
  servoMotor.write(0);
  timeMotor = millis();
  //Timer operando em modo CTC e Com saídas OC1A e OC1B desconectadas
  //Compare Output Mode COM1A = 00 e WGM = 12 = 0xC
  //TIMER COUNTER CONTROL REGISTER A >>>  COM2A|COM2A|COM2B|COM2B|     |     |WGM21|WGM20
  //TIMER COUNTER CONTROL REGISTER B >>>  FOC2A|FOC2B|     |     |WGM22| CS22| CS21| CS20
  //TIMER INTERRUPTION MASK          >>>       |     |     |     |     |OCIEB|OCIEA| TOIE

  TCCR2A  = 0x02;//Modo CTC          >>>    0  |  0  |  0  |  0  |  0  |  0  |  1  |  0
  TCCR2B  = 0x07;// Prescaler 1024   >>>    0  |  0  |  0  |  0  |  0  |  1  |  1  |  1
  //Definindo valor limite para comparação
  OCR2A  = 0x7D;//contagem -->> 125*(125*1024*62,5/1000000000) = 1s
  TCNT2  = 0x00;//iniciando contador
  TIMSK2 = 0x02;//Habilita interrupção do Comparador da Saída A
}

void loop() {
  if(PINB & (1 << PB5)){
    displayPrint();
  }else{
    //buttons control
  	uint8_t curButtons = (PIND & 0x0C) >> 2;//máscara para pegar os pinos PD2 e PD3
  	switch((states >> 1) & 0x03){
      case 0://HORA OFF | MINUTO OFF
  			switch(curButtons){
  				case 3://HORA ON | MINUTO ON
  					if(millis() >= timeButtonHora+0xFA && millis() >= timeButtonMinuto+0xFA){
  						holdButtons = millis();
  						states ^= (1 << 1);
  						states ^= (1 << 2);
              if(telaOn == 0){
                telaOn = TELA;
                PORTB |=  (1 << PB5);//acende LED_BUILTIN
              }
  					}
  					break;
  				case 2://HORA OFF | MINUTO ON
  					if(millis() >= timeButtonMinuto+0xFA){
  						timeButtonMinuto = millis();
              if(states & (1 << 3)){
                clock[0]++;
                if(clock[0] > 9){
                  clock[0] = 0;
                  clock[1]++;
                  if(clock[1] > 5){
                    clock[1] = 0;
                  }
                  if(clock[1] > 5){
                    clock[1] = 0;
                  }
                }
                PORTB |=  (1 << PB5);//acende LED_BUILTIN
              }
              if(telaOn == 0){
                telaOn = TELA;
                PORTB |=  (1 << PB5);//acende LED_BUILTIN
              }
              states ^= (1 << 2);
  					}
  					break;
  				case 1://HORA ON | MINUTO OFF
  					if(millis() >= timeButtonHora+0xFA){
  						timeButtonHora = millis();
              if(states & (1 << 3)){
                clock[2]++;
                if(clock[3] > 1 && clock[2] > 3){
                  clock[2] = 0;
                  clock[3] = 0;
                }else{
                  if(clock[2] > 9){
                    clock[2] = 0;
                    clock[3]++;
                  }
                }
                PORTB |=  (1 << PB5);//acende LED_BUILTIN
              }
              if(telaOn == 0){
                telaOn = TELA;
                PORTB |=  (1 << PB5);//acende LED_BUILTIN
              }
  						states ^= (1 << 1);
  					}
  					break;
  			};
        break;
      case 1://HORA ON  | MINUTO OFF
  			switch(curButtons){
  				case 3://HORA ON | MINUTO ON
  					if(millis() >= timeButtonHora+0xFA && millis() >= timeButtonMinuto+0xFA){
  						holdButtons = millis();
              if(telaOn == 0){
                telaOn = TELA;
                PORTB |=  (1 << PB5);//acende LED_BUILTIN
              }
  						states ^= (1 << 2);
  					}
  					break;
  				case 2://HORA OFF | MINUTO ON
  					if(millis() >= timeButtonMinuto+0xFA){
  						timeButtonMinuto = millis();
              if(states & (1 << 3)){
                clock[2]++;
                if(clock[2] > 9){
                  clock[2] = 0;
                  clock[3]++;
                }
                telaOn = TELA;
                PORTB |=  (1 << PB5);//acende LED_BUILTIN
              }
              if(telaOn == 0){
                telaOn = TELA;
                PORTB |=  (1 << PB5);//acende LED_BUILTIN
              }
  	          states ^= (1 << 1);
  						states ^= (1 << 2);
  					}
            telaOn = 1;
  					break;
  				case 1://HORA ON | MINUTO OFF
  					if(millis() >= timeButtonHora+(0xFA << 1)){
              timeButtonHora = millis();
              if(states & (1 << 3)){
                clock[2]++;
                if(clock[3] > 1 && clock[2] > 3){
                  clock[2] = 0;
                  clock[3] = 0;
                }else{
                  if(clock[2] > 9){
                    clock[2] = 0;
                    clock[3]++;
                  }
                }
                PORTB |=  (1 << PB5);//acende LED_BUILTIN
              }
              if(telaOn == 0){
                telaOn = TELA;
                PORTB |=  (1 << PB5);//acende LED_BUILTIN
              }
            }
  					break;
  				case 0:
  					states ^= (1 << 1);
  					break;
  			};
        break;
      case 2://HORA OFF | MINUTO ON
  			switch(curButtons){
  				case 3:
  					if(millis() >= timeButtonHora+0xFA && millis() >= timeButtonMinuto+0xFA){
  						holdButtons = millis();
              if(telaOn == 0){
                telaOn = TELA;
                PORTB |=  (1 << PB5);//acende LED_BUILTIN
              }
  						states ^= (1 << 1);
  					}
  					break;
  				case 2:
            if(millis() >= timeButtonMinuto+(0xFA << 1)){
              timeButtonMinuto = millis();
              if(states & (1 << 3)){
                clock[0]++;
                if(clock[0] > 9){
                  clock[0] = 0;
                  clock[1]++;
                  if(clock[1] > 5){
                    clock[1] = 0;
                  }
                }
                PORTB |=  (1 << PB5);//acende LED_BUILTIN
              }
              if(telaOn == 0){
                telaOn = TELA;
                PORTB |=  (1 << PB5);//acende LED_BUILTIN
              }
            }
  					break;
  				case 1:
  					if(millis() >= timeButtonHora+0xFA){
  						timeButtonHora = millis();
              if(states & (1 << 3)){
                clock[2]++;
                if(clock[3] > 1 && clock[2] > 3){
                  clock[2] = 0;
                  clock[3] = 0;
                }else{
                  if(clock[2] > 9){
                    clock[2] = 0;
                    clock[3]++;
                  }
                }
                PORTB |=  (1 << PB5);//acende LED_BUILTIN
              }
              if(telaOn == 0){
                telaOn = TELA;
                PORTB |=  (1 << PB5);//acende LED_BUILTIN
              }
  	          states ^= (1 << 1);
  						states ^= (1 << 2);
  					}
  					break;
  				case 0:
  					states ^= (1 << 2);
  					break;
  			};
        break;
      case 3://HORA ON  | MINUTO ON
  			switch(curButtons){
  				case 0:
  					if(millis() >= holdButtons+ (0xFA << 2)){
  	          states ^= (1 << 3);
              if(!(states & (1 << 3))){
                segundo = 0;
              }
              PORTB |=  (1 << PB5);//acende LED_BUILTIN
  	        }
  					states ^= (1 << 1);
  					states ^= (1 << 2);
            timeButtonHora   = millis();
            timeButtonMinuto = millis();
  					break;
  				case 1:
  					if(millis() >= holdButtons+ (0xFA << 2)){
  	          states ^= (1 << 3);
              if(!(states & (1 << 3))){
                segundo = 0;
              }
              PORTB |=  (1 << PB5);//acende LED_BUILTIN
  	        }
            if(telaOn == 0){
              telaOn = TELA;
              PORTB |=  (1 << PB5);//acende LED_BUILTIN
            }
  					states ^= (1 << 1);
            timeButtonHora   = millis();
            timeButtonMinuto = millis();
  					break;
  				case 2:
  					if(millis() >= holdButtons+ (0xFA << 2)){
  	          states ^= (1 << 3);
              if(!(states & (1 << 3))){
                segundo = 0;
              }
              PORTB |=  (1 << PB5);//acende LED_BUILTIN
  	        }
            if(telaOn == 0){
              telaOn = TELA;
              PORTB |=  (1 << PB5);//acende LED_BUILTIN
            }
  					states ^= (1 << 2);
            timeButtonHora   = millis();
            timeButtonMinuto = millis();
  					break;
  			};
  			break;
    };
    if(~PIND & (1 << PD4)){
      states |= (1 << 0);//ativa bit para ativação do motor
    }
    //Detectando vibrações
    int32_t vibration = pulseIn(5,HIGH);
    if(vibration >= 10000){
      states |= (1 << 0);//ativa bit para ativação do motor
    }
    //verifica comparador analógico.
    if(~ACSR & (1 << ACO)){
      states |= (1 << 0);//ativa bit para ativação do motor
    }
    //Ação do motor a cada 500ms
    if(states & (1 << 0) && millis() >= timeMotor+(0xFA << 1)){
      timeMotor = millis();
      if(servoMotor.read()){
        servoMotor.write(0);
      }else{
        servoMotor.write(180);
      }
      if(telaOn == 0){
        telaOn = TELA;
        PORTB |=  (1 << PB5);//acende LED_BUILTIN
      }
      states &= ~(1 << 0);
    }
  }
}
//Rotina de interrupção para contagem dos segundos e controle do relógio
ISR(TIMER2_COMPA_vect){
  TCNT2 = 0x00;// Reinicializa o registrador do Timer2
  seg++;
  if(seg > 124){
    seg = 0;
    segundo++;
    if(segundo > 59){
      segundo = 0;
      if(telaOn){
        telaOn--;
        if(!telaOn){
          PORTB |=  (1 << PB5);//acende LED_BUILTIN}
        }
      }
      if(!(states & (1 << 3))){
        switch (clock[0]){
        case 0:
        case 1:
        case 2:
        case 3:
        case 4:
        case 5:
        case 6:
        case 7:
        case 8:
          //unidades dos minutos
          clock[0]++;
          break;
        default:
          switch (clock[1]){
            case 0:
            case 1:
            case 2:
            case 3:
            case 4:
              //dezenas dos minutos
              clock[0]=0;
              clock[1]++;
              break;
            default:
              clock[0] = 0;//zera minutos
              clock[1] = 0;
              switch (clock[2]){
                case 0:
                case 1:
                case 2:
                case 3:
                  if(clock[3] > 1){
                    clock[2] = 0;
                    clock[3] = 0;
                    break;
                  }//verifica se maior que 23 horas
                case 4:
                case 5:
                case 6:
                case 7:
                case 8:
                  //unidades das horas
                  clock[2]++;
                  break;
                default:
                  switch (clock[3]){
                    clock[2] = 0;
                    clock[3]++;//dezenas das horas
                    break;
                  };
                  break;
              };
              break;
          };
          break;
        };
        PORTB |=  (1 << PB5);//acende LED_BUILTIN}
      }
    }
  }
}

// code stored in the sketch: tarefa03.ino
#include <Arduino.h>
#include <Wire.h>
#include <Servo.h>
#include <LiquidCrystal_I2C.h>

//LCD I2C for display delay LED and state
LiquidCrystal_I2C i2cLcd(0x27,2,1,0,4,5,6,7,3,POSITIVE);
//Servo:
Servo servoMotor;
//interval | oldInfrared | atualizarLcd | oldMotor
uint8_t states = B11111000;
int32_t vibrationValue = 0;
uint64_t timeAction;//para manter um intervalo entre cada operação verificada

void displayPrint(void){
  PORTB ^= (1 << PB5);//faz LED_BUILTIN piscar
  String msg = "VB:";
  if(vibrationValue < 100000){
    msg += "0";
  }
  if(vibrationValue < 10000){
    msg += "0";
  }
  if(vibrationValue < 1000){
    msg += "0";
  }
  if(vibrationValue < 100){
    msg += "0";
  }
  if(vibrationValue < 10){
    msg += "0";
  }
  msg += vibrationValue;
  msg += "Hz|";
  if(states & B00000100){
    msg += " IR:SIM ";
  }else{
    msg += " IR:NAO ";
  }
  i2cLcd.setCursor(0,3);
  i2cLcd.print(msg);
  Serial.print(msg);
  Serial.println();
  PORTB ^= (1 << PB5);//faz LED_BUILTIN piscar
}

void setup() {
  DDRD  &= ~(1 << PD2);PORTD &= ~(1 << PD2);//pinMode(2,INPUT);//infrared sensor
  DDRD  &= ~(1 << PD3);PORTD &= ~(1 << PD3);//pinMode(3,INPUT);//vibration sensor
  DDRB  |=  (1 << PB5);PORTB &= ~(1 << PB5);//pinMode(13,OUTPUT);digitalWrite(13,LOW);//LED_BUILTIN
  ACSR   = 0;//ativar comparador analógico
  servoMotor.attach(9);//define servo motor PWM no pino 9
  i2cLcd.begin(20,4);
  i2cLcd.clear();
  Serial.begin(115200);
  i2cLcd.setCursor(0,0);
  i2cLcd.print(" Wellington Rodrigo ");
  Serial.print(" Wellington Rodrigo ");
  Serial.println();
  i2cLcd.setCursor(0,1);
  i2cLcd.print(" Software Embarcado ");
  Serial.print(" Software Embarcado ");
  Serial.println();
  i2cLcd.setCursor(0,2);
  i2cLcd.print("     TAREFA  03     ");
  Serial.print("     TAREFA  03     ");
  Serial.println();
  displayPrint();
  servoMotor.write(0);
  timeAction = millis();
}

void loop() {

  if(millis() >= timeAction+((states & B11111100) << 1)){
    timeAction = millis();
    uint8_t curStates = 0;
    //Detectando obstáculo com sensor infravermelho
    curStates = (~PIND & B00000100);//máscara para pegar o pino PD2 Infrared
    if(curStates ^ (states & (1 << 2))){
      states ^= (1 << 2);//atualiza somente se o valor mudou
      states |= (1 << 1);//habilita atualização do display
    }
    //Detectando vibrações
    int32_t vibration = vibrationValue;
    vibrationValue = pulseIn(3,HIGH);
  	if(vibrationValue != vibration){
      states |= (1 << 1);//habilita atualização do display
  	}
    if(vibrationValue >=10000){
      curStates |= (1 << 1);//se maior que 10000 ativa bit indicando sua ativação
    }
    //verifica comparador analógico.
    if(~ACSR & (1 << ACO)){
      curStates |= (1 << 0);//ativa bit indicando sua ativação
    }
    //verifica se precisa atualizar o display
    if(states & (1 << 1)){
      displayPrint();
      states &= ~(1 << 1);
    }
    //verifica se o motor deve ser acionado
    if(curStates > 0){
      states ^= (1 << 0);
      if(states & (1 << 0)){
       servoMotor.write(180);
      }else{
       servoMotor.write(0);
      }
    }
  }
}
