# Fritzing sketch tarefa05 (saved by Fritzing 0.9.3b)
breadboards: 1

parts:
  Componente1 = Arduino Uno (Rev3)
  S1 = Pushbutton [package="[THT]"]
  S2 = Pushbutton [package="[THT]"]
  LED2 = LED - 5mm [color="Red (633nm)" package="5 mm [THT]"]
  LED3 = LED - 5mm [color="Red (633nm)" package="5 mm [THT]"]
  R2 = Resistor [tolerance=±5% resistance=330k package=THT]
  R3 = Resistor [tolerance=±5% resistance=330k package=THT]
  LCM1602_IIC2 = LCM1602 IIC [part_number="LCM1602 IIC" chip_label="LCM1602 IIC" package="DIP (Dual Inline) [THT]"]
  LCD2 = LCD screen

nets:
  N1: Componente1.A4/SDA, LCM1602_IIC2.SDA
  N2: Componente1.A5/SCL, LCM1602_IIC2.SCL
  GND: Componente1.GND, R2.Pin_0, R3.Pin_0, LCM1602_IIC2.GND
  N3: Componente1.D2, S1.Pin_1, S1.Pin_2, LED2.anode
  N4: Componente1.D3_PWM, S2.Pin_1, S2.Pin_2, LED3.anode
  5V: Componente1.5V, S1.Pin_3, S1.Pin_4, S2.Pin_3, S2.Pin_4, LCM1602_IIC2.VCC
  N5: LED2.cathode, R3.Pin_1
  N6: LED3.cathode, R2.Pin_1
  VSS: LCM1602_IIC2.VSS, LCD2.VSS
  VDD: LCM1602_IIC2.VDD, LCD2.VDD
  N7: LCM1602_IIC2.V0, LCD2.V0
  N8: LCM1602_IIC2.RS, LCD2.RS
  N9: LCM1602_IIC2.RW, LCD2.R/W
  N10: LCM1602_IIC2.E, LCD2.E
  N11: LCM1602_IIC2.D0, LCD2.DB0
  N12: LCM1602_IIC2.D1, LCD2.DB1
  N13: LCM1602_IIC2.D2, LCD2.DB2
  N14: LCM1602_IIC2.D3, LCD2.DB3
  N15: LCM1602_IIC2.D4, LCD2.DB4
  N16: LCM1602_IIC2.D5, LCD2.DB5
  N17: LCM1602_IIC2.D6, LCD2.DB6
  N18: LCM1602_IIC2.D7, LCD2.DB7
  N19: LCM1602_IIC2.A, LCD2.LED+
  N20: LCM1602_IIC2.K, LCD2.LED-
  N21: LCM1602_IIC2.LED_A, LCM1602_IIC2.LED_B

custom parts:
  LCM1602 IIC: I2C-Module to use a 1602 or 2004 LCD on with the wire.h libory Serial LCD Modul

// code stored in the sketch: tarefa01.ino
#include <Arduino.h>
#include <Wire.h>
#include <LiquidCrystal_I2C.h>
//LCD I2C for display delay LED and state
LiquidCrystal_I2C i2cLcd(0x27,2,1,0,4,5,6,7,3,POSITIVE);
//debaunce | LOCK LED | oldStateUp | oldStateDown
uint8_t states = B11111000;
uint64_t timeLed;
uint16_t delayLed = 1000;//milliseconds
uint64_t timeButtonDown;
uint64_t timeButtonUp;
uint64_t holdButtons;

void displayPrint(void){
	String 	msg = "";
  if(states & (1 << 2)){
    msg += "    LOCK LED: ";
    if(PINB & (1 << PB0)){
      msg += "ON    ";
    }else{
      msg += "OFF   ";
    }
  }else{
    msg += "DELAY LED: ";
  	if(delayLed < 10000){
  		msg += "0";
  	}
  	if(delayLed < 10000){
  		msg += "0";
  	}
  	if(delayLed < 1000){
  		msg += "0";
  	}
  	if(delayLed < 100){
  		msg += "0";
  	}
  	if(delayLed < 10){
  		msg += "0";
  	}
  	msg += delayLed;
  	msg += "ms ";
  }
  i2cLcd.setCursor(0,3);
  i2cLcd.print(msg);
  Serial.print(msg);
  Serial.println();
}

void setup() {
  DDRD  &= ~(1 << PD2);PORTD &= ~(1 << PD2);//pinMode(2,INPUT);//button DOWN delay LED
  DDRD  &= ~(1 << PD3);PORTD &= ~(1 << PD3);//pinMode(4,INPUT);//button UP delay LED
	DDRB  &= ~(1 << PB0);PORTB &= ~(1 << PB0);//pinMode(8,OUTPUT);digitalWrite(8,LOW);//set LED to LOW
  i2cLcd.begin(20,4);
  i2cLcd.clear();
  Serial.begin(115200);
  i2cLcd.setCursor(0,0);
  i2cLcd.print(" Wellington Rodrigo ");
  Serial.print(" Wellington Rodrigo ");
  Serial.println();
  i2cLcd.setCursor(0,1);
  i2cLcd.print(" Software Embarcado ");
  Serial.print(" Software Embarcado ");
  Serial.println();
  i2cLcd.setCursor(0,2);
  i2cLcd.print("     TAREFA  01     ");
  Serial.print("     TAREFA  01     ");
  Serial.println();
  displayPrint();
	timeLed = millis();
}

void loop() {
  while(states & (1 << 2));//caso seja setado para true trava a execução
  if(millis() >= timeLed+delayLed){
    timeLed = millis();
		//faz o LED piscar
		PORTB ^= (1 << PB0);//ledState = ~ledState;digitalWrite(8,ledState);
  }
  //buttons control
	uint8_t curButtons = (PIND & B00001100) >> 2;//máscara para pegar os pinos PD2 e PD3
	switch(states & B00000011){
    case 0://DOWN OFF | UP OFF
			switch(curButtons){
				case 3:
					if(millis() >= timeButtonDown+((states & B11111000) >> 2) && millis() >= timeButtonDown+((states & B11111000) >> 2)){
						holdButtons = millis();
						states ^= (1 << 0);
						states ^= (1 << 1);
					}
					break;
				case 2:
					if(millis() >= timeButtonDown+((states & B11111000) >> 2)){
						timeButtonUp = millis();
						if(delayLed < 10000){
							delayLed += 100;
						}
						displayPrint();
						states ^= (1 << 1);
					}
					break;
				case 1:
					if(millis() >= timeButtonDown+((states & B11111000) >> 2)){
						timeButtonDown = millis();
						if(delayLed > 100){
							delayLed -= 100;
						}
						displayPrint();
						states ^= (1 << 0);
					}
					break;
			};
      break;
    case 1://DOWN ON  | UP OFF
			switch(curButtons){
				case 3:
					if(millis() >= timeButtonDown+((states & B11111000) >> 2) && millis() >= timeButtonDown+((states & B11111000) >> 2)){
						holdButtons = millis();
						states ^= (1 << 1);
					}
					break;
				case 2:
					if(millis() >= timeButtonDown+((states & B11111000) >> 2)){
						timeButtonUp = millis();
						if(delayLed < 10000){
							delayLed += 100;
						}
						displayPrint();
	          states ^= (1 << 0);
						states ^= (1 << 1);
					}
					break;
				case 1:
					if(millis() >= timeButtonDown+(states & B11111000)){
            timeButtonDown = millis();
	          if(delayLed > 100){
							delayLed -= 100;
						}
						displayPrint();
          }
					break;
				case 0:
					states ^= (1 << 0);
					break;
			};
      break;
    case 2://DOWN OFF | UP ON
			switch(curButtons){
				case 3:
					if(millis() >= timeButtonDown+((states & B11111000) >> 2) && millis() >= timeButtonDown+((states & B11111000) >> 2)){
						holdButtons = millis();
						states ^= (1 << 0);
					}
					break;
				case 2:
          if(millis() >= timeButtonUp+(states & B11111000)){
            timeButtonUp = millis();
	          if(delayLed < 10000){
							delayLed += 100;
						}
						displayPrint();
          }
					break;
				case 1:
					if(millis() >= timeButtonUp+((states & B11111000) >> 2)){
						timeButtonDown = millis();
						if(delayLed < 10000){
							delayLed -= 100;
						}
						displayPrint();
	          states ^= (1 << 0);
						states ^= (1 << 1);
					}
					break;
				case 0:
					states ^= (1 << 1);
					break;
			};
      break;
    case 3://DOWN ON  | UP ON
			switch(curButtons){
				case 0:
					if(millis()>=holdButtons+500){
	          states |= (1 << 2);
						displayPrint();
	        }
					states ^= (1 << 0);
					states ^= (1 << 1);
					break;
				case 1:
					if(millis()>=holdButtons+500){
	          states |= (1 << 2);
						displayPrint();
	        }
					states ^= (1 << 0);
					break;
				case 2:
					if(millis()>=holdButtons+500){
	          states |= (1 << 2);
						displayPrint();
	        }
					states ^= (1 << 1);
					break;
			};
			break;
  };
}

// code stored in the sketch: tarefa05.ino
/* Cáculo para estouro do timer
 * Estouro = Timer2_cont x prescaler x ciclo de máquina
 * Ciclo de máquina = 1/Fosc = 1/16E6 = 62,5ns = 62,5E-9s
 * Estouro = 156 x 1024 x 62,5E-9 = 9,984000
*/
#include <Arduino.h>
#include <Wire.h>
#include <LiquidCrystal_I2C.h>

//LCD I2C for display delay LED and states
LiquidCrystal_I2C i2cLcd(0x27,2,1,0,4,5,6,7,3,POSITIVE);

uint64_t timeClock;
uint64_t timeButtonHora;
uint64_t timeButtonMinuto;
uint64_t holdButtons;
//interval | SET CLOCK | oldStateMinuto | oldStateHora
uint8_t states   = B11111000;
uint8_t hora     = 0;
uint8_t minuto   = 0;
uint8_t segundo  = 0;
uint8_t msegundo = 0;//max 100*10

void displayPrint(void){
  PORTB ^= (1 << PB5);//faz LED_BUILTIN piscar
  String msg=" ";
  if(hora < 10){
    msg += "0";
  }
  msg += hora;
  msg += ":";
  if(minuto < 10){
    msg += "0";
  }
  msg += minuto;
  msg += ":";
  if(segundo < 10){
    msg += "0";
  }
  msg += segundo;
  if(states & (1 << 2)){
    msg += "  SETTING  ";
  }else{
    msg += ":";
    if(msegundo < 100){
      msg += "0";
    }
    if(msegundo < 10){
      msg += "0";
    }
    msg += msegundo;
    msg += "0";
  }
  i2cLcd.setCursor(0,3);
  i2cLcd.print(msg);
  Serial.print(msg);
  Serial.println();
  PORTB ^= (1 << PB5);//faz LED_BUILTIN piscar
}

void setup() {
  DDRD  &= ~(1 << PD2);PORTD &= ~(1 << PD2);//pinMode(2,INPUT);//botao da hora
  DDRD  &= ~(1 << PD3);PORTD &= ~(1 << PD3);//pinMode(4,INPUT);//botao do minuto
  DDRB  |=  (1 << PB5);PORTB &= ~(1 << PB5);//pinMode(13,OUTPUT);digitalWrite(13,LOW);//LED_BUILTIN
  //Timer operando em modo CTC e Set OC1A COM1A:11 -
  //Compare Output Mode COM 11=3
  TCCR1A |=  (1 << COM1A0);
  TCCR1A |=  (1 << COM1A1);
  //Waveform Generation Mode WGM 010=2
  TCCR1A &= ~(1 << WGM10);
  TCCR1A |=  (1 << WGM11);
  TCCR1B &= ~(1 << WGM12);

  //definindo prescaler para 1024 CS:101
  TCCR1B |=  (1 << CS10);
  TCCR1B &= ~(1 << CS11);
  TCCR1B |=  (1 << CS12);
  //Definindo valor limite para comparação
  OCR1A = 156; //contagem -->> 156*1024*62,5/1000000000 = 0,009984s = 9,984ms

  i2cLcd.begin(20,4);
  i2cLcd.clear();
  Serial.begin(115200);
  i2cLcd.setCursor(0,0);
  i2cLcd.print(" Wellington Rodrigo ");
  Serial.print(" Wellington Rodrigo ");
  Serial.println();
  i2cLcd.setCursor(0,1);
  i2cLcd.print(" Software Embarcado ");
  Serial.print(" Software Embarcado ");
  Serial.println();
  i2cLcd.setCursor(0,2);
  i2cLcd.print("     TAREFA  05     ");
  Serial.print("     TAREFA  05     ");
  Serial.println();
  displayPrint();
  //Limpa a flag Output Compare A Match Flag
  TIFR1  |=  (1 << OCF1A);
  timeClock = millis();
}

void loop() {

  //buttons control
	uint8_t curButtons = (PIND & B00001100) >> 2;//máscara para pegar os pinos PD2 e PD3
	switch(states & B00000011){
    case 0://HORA OFF | MINUTO OFF
			switch(curButtons){
				case 3:
					if(millis() >= timeButtonHora+((states & B11111000) >> 1) && millis() >= timeButtonHora+((states & B11111000) >> 1)){
						holdButtons = millis();
						states ^= (1 << 0);
						states ^= (1 << 1);
					}
					break;
				case 2:
					if(millis() >= timeButtonHora+((states & B11111000) >> 1)){
						timeButtonMinuto = millis();
            if(states & (1 << 2)){
              minuto++;
              if(minuto > 59){
                minuto = 0;
              }
						  displayPrint();
            }
            states ^= (1 << 1);
					}
					break;
				case 1:
					if(millis() >= timeButtonHora+((states & B11111000) >> 1)){
						timeButtonHora = millis();
            if(states & (1 << 2)){
              hora++;
              if(hora > 23){
                hora = 0;
              }
              displayPrint();
            }
						states ^= (1 << 0);
					}
					break;
			};
      break;
    case 1://HORA ON  | MINUTO OFF
			switch(curButtons){
				case 3:
					if(millis() >= timeButtonHora+((states & B11111000) >> 1) && millis() >= timeButtonHora+((states & B11111000) >> 1)){
						holdButtons = millis();
						states ^= (1 << 1);
					}
					break;
				case 2:
					if(millis() >= timeButtonHora+((states & B11111000) >> 1)){
						timeButtonMinuto = millis();
            if(states & (1 << 2)){
              minuto++;
              if(minuto > 59){
                minuto = 0;
              }
  						displayPrint();
            }
	          states ^= (1 << 0);
						states ^= (1 << 1);
					}
					break;
				case 1:
					if(millis() >= timeButtonHora+(states & B11111000)){
            timeButtonHora = millis();
            if(states & (1 << 2)){
              hora++;
              if(hora > 23){
                hora = 0;
              }
  						displayPrint();
            }
          }
					break;
				case 0:
					states ^= (1 << 0);
					break;
			};
      break;
    case 2://HORA OFF | MINUTO ON
			switch(curButtons){
				case 3:
					if(millis() >= timeButtonHora+((states & B11111000) >> 1) && millis() >= timeButtonHora+((states & B11111000) >> 1)){
						holdButtons = millis();
						states ^= (1 << 0);
					}
					break;
				case 2:
          if(millis() >= timeButtonMinuto+(states & B11111000)){
            timeButtonMinuto = millis();
            if(states & (1 << 2)){
              minuto++;
              if(minuto > 59){
                minuto = 0;
              }
  						displayPrint();
            }
          }
					break;
				case 1:
					if(millis() >= timeButtonMinuto+((states & B11111000) >> 1)){
						timeButtonHora = millis();
            if(states & (1 << 2)){
              hora++;
              if(hora > 23){
                hora = 0;
              }
  						displayPrint();
            }
	          states ^= (1 << 0);
						states ^= (1 << 1);
					}
					break;
				case 0:
					states ^= (1 << 1);
					break;
			};
      break;
    case 3://HORA ON  | MINUTO ON
			switch(curButtons){
				case 0:
					if(millis() >= holdButtons+ ((states & B11111000) << 1)){
	          states ^= (1 << 2);
						displayPrint();
	        }
					states ^= (1 << 0);
					states ^= (1 << 1);
          timeClock        = millis();
          timeButtonHora   = millis();
          timeButtonMinuto = millis();
					break;
				case 1:
					if(millis() >= holdButtons+ ((states & B11111000) << 1)){
	          states ^= (1 << 2);
						displayPrint();
            timeClock = millis();
	        }
					states ^= (1 << 0);
          timeClock        = millis();
          timeButtonHora   = millis();
          timeButtonMinuto = millis();
					break;
				case 2:
					if(millis() >= holdButtons+ ((states & B11111000) << 1)){
	          states ^= (1 << 2);
						displayPrint();
            timeClock = millis();
	        }
					states ^= (1 << 1);
          timeClock        = millis();
          timeButtonHora   = millis();
          timeButtonMinuto = millis();
					break;
			};
			break;
  };
  if(TIFR1 & (1 << OCF1A)){
    //Limpa a flag Output Compare A Match Flag
    TIFR1  |=  (1 << OCF1A);
    msegundo++;
    if(msegundo > 99){
      msegundo = 0;
      segundo++;
    }
    if(segundo > 59){
      segundo = 0;
      minuto++;
    }
		if(minuto > 59){
			minuto = 0;
			hora++;
		}
		if(hora > 23){
			hora = 0;
		}
    displayPrint();
  }
  // if(~states & (1 << 2) && millis() >= timeClock+1000){
  //   timeClock = millis();
  //   segundo++;
  //   if(segundo >59){
  //     segundo = 0;
  //     minuto++;
  //   }
	// 	if(minuto > 59){
	// 		minuto = 0;
	// 		hora++;
	// 	}
	// 	if(hora > 23){
	// 		hora = 0;
	// 	}
	// 	displayPrint();
  // }
}

// code stored in the sketch: trabalho01.ino
#include <Arduino.h>
#include <Wire.h>
#include <LiquidCrystal_I2C.h>
//LCD I2C for display delay LED and state
LiquidCrystal_I2C i2cLcd(0x27,2,1,0,4,5,6,7,3,POSITIVE);
//debaunce | LOCK LED | oldStateUp | oldStateDown
uint8_t states = 0;
uint64_t timeLed;
uint16_t delayLed = 1000;//milliseconds
uint64_t timeButtonDown;
uint64_t timeButtonUp;
uint64_t holdButtons;

void delayLedPrint(void){
	String 	msg = "";
  if(states & (1 << 2)){
    msg += "    LOCK LED: ";
    if(PINB & (1 << PB0)){
      msg += "ON    ";
    }else{
      msg += "OFF   ";
    }
  }else{
    msg += "DELAY LED: ";
  	if(delayLed < 10000){
  		msg += "0";
  	}
  	if(delayLed < 10000){
  		msg += "0";
  	}
  	if(delayLed < 1000){
  		msg += "0";
  	}
  	if(delayLed < 100){
  		msg += "0";
  	}
  	if(delayLed < 10){
  		msg += "0";
  	}
  	msg += delayLed;
  	msg += "ms ";
  }
  i2cLcd.setCursor(0,3);
  i2cLcd.print(msg);
  Serial.print(msg);
  Serial.println();
  timeLed = millis();
}

void setup() {
  DDRD  &= ~(1 << PD2);PORTD &= ~(1 << PD2);//pinMode(2,INPUT);//button DOWN delay LED
  DDRD  &= ~(1 << PD4);PORTD &= ~(1 << PD4);//pinMode(4,INPUT);//button UP delay LED
	DDRB  &= ~(1 << PB0);PORTB &= ~(1 << PB0);//pinMode(8,OUTPUT);digitalWrite(8,LOW);//set LED to LOW
  i2cLcd.begin(20,4);
  i2cLcd.clear();
  Serial.begin(115200);
  i2cLcd.setCursor(0,0);
  i2cLcd.print(" Wellington Rodrigo ");
  Serial.print(" Wellington Rodrigo ");
  Serial.println();
  i2cLcd.setCursor(0,1);
  i2cLcd.print(" Software Embarcado ");
  Serial.print(" Software Embarcado ");
  Serial.println();
  i2cLcd.setCursor(0,2);
  i2cLcd.print("     TAREFA  01     ");
  Serial.print("     TAREFA  01     ");
  Serial.println();
  delayLedPrint();
  //inicia ativando todos os bits para do debaunce  248ms
  states = (1 << 7) | (1 << 6) | (1 << 5) | (1 << 4) | (1 << 3);
}

void loop() {
  while(states & (1 << 2));//caso seja setado para true trava a execução
  if(millis() >= timeLed+delayLed){
    timeLed = millis();
		//faz o LED piscar
		PORTB ^= (1 << PB0);//ledState = ~ledState;digitalWrite(8,ledState);
  }
  //buttons control
	uint8_t curButtons = (PIND & B00001100) >> 2;//máscara para pegar os pinos PD2 e PD3
	switch(states & B00000011){
    case 0://DOWN OFF | UP OFF
			switch(curButtons){
				case 3:
					if(millis() >= timeButtonDown+((states & B11111000) >> 2) && millis() >= timeButtonDown+((states & B11111000) >> 2)){
						holdButtons = millis();
						states ^= (1 << 0);
						states ^= (1 << 1);
					}
					break;
				case 2:
					if(millis() >= timeButtonDown+((states & B11111000) >> 2)){
						timeButtonUp = millis();
						if(delayLed < 10000){
							delayLed += 100;
						}
						delayLedPrint();
						states ^= (1 << 1);
					}
					break;
				case 1:
					if(millis() >= timeButtonDown+((states & B11111000) >> 2)){
						timeButtonDown = millis();
						if(delayLed > 100){
							delayLed -= 100;
						}
						delayLedPrint();
						states ^= (1 << 0);
					}
					break;
			};
      break;
    case 1://DOWN ON  | UP OFF
			switch(curButtons){
				case 3:
					if(millis() >= timeButtonDown+((states & B11111000) >> 2) && millis() >= timeButtonDown+((states & B11111000) >> 2)){
						holdButtons = millis();
						states ^= (1 << 1);
					}
					break;
				case 2:
					if(millis() >= timeButtonDown+((states & B11111000) >> 2)){
						timeButtonUp = millis();
						if(delayLed < 10000){
							delayLed += 100;
						}
						delayLedPrint();
	          states ^= (1 << 0);
						states ^= (1 << 1);
					}
					break;
				case 1:
					if(millis() >= timeButtonDown+(states & B11111000)){
            timeButtonDown = millis();
	          if(delayLed > 100){
							delayLed -= 100;
						}
						delayLedPrint();
          }
					break;
				case 0:
					states ^= (1 << 0);
					break;
			};
      break;
    case 2://DOWN OFF | UP ON
			switch(curButtons){
				case 3:
					if(millis() >= timeButtonDown+((states & B11111000) >> 2) && millis() >= timeButtonDown+((states & B11111000) >> 2)){
						holdButtons = millis();
						states ^= (1 << 0);
					}
					break;
				case 2:
          if(millis() >= timeButtonUp+(states & B11111000)){
            timeButtonUp = millis();
	          if(delayLed < 10000){
							delayLed += 100;
						}
						delayLedPrint();
          }
					break;
				case 1:
					if(millis() >= timeButtonUp+((states & B11111000) >> 2)){
						timeButtonDown = millis();
						if(delayLed < 10000){
							delayLed -= 100;
						}
						delayLedPrint();
	          states ^= (1 << 0);
						states ^= (1 << 1);
					}
					break;
				case 0:
					states ^= (1 << 1);
					break;
			};
      break;
    case 3://DOWN ON  | UP ON
			switch(curButtons){
				case 0:
					if(millis()>=holdButtons+500){
	          states |= (1 << 2);
						delayLedPrint();
	        }
					states ^= (1 << 0);
					states ^= (1 << 1);
					break;
				case 1:
					if(millis()>=holdButtons+500){
	          states |= (1 << 2);
						delayLedPrint();
	        }
					states ^= (1 << 0);
					break;
				case 2:
					if(millis()>=holdButtons+500){
	          states |= (1 << 2);
						delayLedPrint();
	        }
					states ^= (1 << 1);
					break;
			};
			break;
  };
}
